// Logisim project SAP2.circ as structural Verilog: 13 circuits, main circuit main
module main (
  input  in_1,
  input  in_2,
  input  [15:0] Tester,
  input  Manual,
  input  in_5,
  input  in_6,
  input  in_7,
  input  in_8,
  input  in_9,
  input  in_10,
  input  in_11,
  input  in_12,
  input  in_13,
  input  in_14,
  input  in_15,
  input  in_16,
  input  in_17,
  input  in_18,
  input  in_19,
  input  [3:0] in_20,
  input  in_21,
  input  in_22,
  input  in_23,
  input  in_24,
  input  in_25,
  input  in_26,
  input  in_27,
  input  in_28,
  input  in_29,
  input  in_30,
  output [15:0] Bus,
  output [15:0] Program_Counter,
  output [7:0] Accumulator,
  output [15:0] MAR,
  output [7:0] ALU_Output,
  output [7:0] TMP,
  output [7:0] B,
  output [7:0] MDR,
  output [7:0] C,
  output [7:0] Instruction_Register,
  output [3:0] out_41
);

  wire AI, ALUM, ALUO, AO, BI, BO, CI, clock_1_out, CLR, CO, DCLR, DO, H, IRI, MARI, MARO, MDRI, MDRM, MDRO,
       NF, not_1_out, PCA, PCI, PCO, Pulse_out, Reset_PC_out, RI, RO, TI, TO, ZF;
  wire [3:0] ALUC, Output_lsb, Output_msb;
  wire [7:0] mdr_1_ramout, ram_1_data;
  wire [15:0] alu_1_output, buffer_2_out, buffer_3_out, buffer_5_out, buffer_6_out, buffer_7_out,
       buffer_9_out, buffer_12_out, buffer_14_out, buffer_16_out, mar_1_out, mdr_1_busout,
       n16_bit_register_1_out, n16_bit_register_2_out, n16_bit_register_3_out, n16_bit_register_4_out,
       programcounter_1_out_2;
  wire [28:0] control_logic_1_controlout;
  wire [31:0] Output_bcd;

  assign PCI = Manual ? in_5 : 1'bz;  // Controlled_Buffer controlled_buffer_1
  assign PCA = Manual ? in_6 : 1'bz;  // Controlled_Buffer controlled_buffer_2
  assign PCO = Manual ? in_7 : 1'bz;  // Controlled_Buffer controlled_buffer_3
  assign MARI = Manual ? in_8 : 1'bz;  // Controlled_Buffer controlled_buffer_4
  assign MARO = Manual ? in_9 : 1'bz;  // Controlled_Buffer controlled_buffer_5
  assign RI = Manual ? in_10 : 1'bz;  // Controlled_Buffer controlled_buffer_6
  assign RO = Manual ? in_11 : 1'bz;  // Controlled_Buffer controlled_buffer_7
  assign MDRI = Manual ? in_12 : 1'bz;  // Controlled_Buffer controlled_buffer_8
  assign MDRM = Manual ? in_13 : 1'bz;  // Controlled_Buffer controlled_buffer_9
  assign MDRO = Manual ? in_14 : 1'bz;  // Controlled_Buffer controlled_buffer_10
  assign IRI = Manual ? in_15 : 1'bz;  // Controlled_Buffer controlled_buffer_11
  assign CLR = Manual ? in_16 : 1'bz;  // Controlled_Buffer controlled_buffer_12
  assign AO = Manual ? in_17 : 1'bz;  // Controlled_Buffer controlled_buffer_13
  assign AI = Manual ? in_18 : 1'bz;  // Controlled_Buffer controlled_buffer_14
  assign ALUM = Manual ? in_19 : 1'bz;  // Controlled_Buffer controlled_buffer_15
  assign ALUC = Manual ? in_20 : 4'bz;  // Controlled_Buffer controlled_buffer_16
  assign ALUO = Manual ? in_21 : 1'bz;  // Controlled_Buffer controlled_buffer_17
  assign TO = Manual ? in_22 : 1'bz;  // Controlled_Buffer controlled_buffer_18
  assign TI = Manual ? in_23 : 1'bz;  // Controlled_Buffer controlled_buffer_19
  assign BO = Manual ? in_24 : 1'bz;  // Controlled_Buffer controlled_buffer_20
  assign BI = Manual ? in_25 : 1'bz;  // Controlled_Buffer controlled_buffer_21
  assign CO = Manual ? in_26 : 1'bz;  // Controlled_Buffer controlled_buffer_22
  assign CI = Manual ? in_27 : 1'bz;  // Controlled_Buffer controlled_buffer_23
  assign DO = Manual ? in_28 : 1'bz;  // Controlled_Buffer controlled_buffer_24
  assign DCLR = Manual ? in_29 : 1'bz;  // Controlled_Buffer controlled_buffer_25
  assign H = Manual ? in_30 : 1'bz;  // Controlled_Buffer controlled_buffer_26
  MDR mdr_1 (
    .BUSIn(buffer_5_out), .RAMIn(ram_1_data), .BUSOut(mdr_1_busout), .RAMOut(mdr_1_ramout), .Load(MDRI),
    .Enable(MDRO), .State(MDR), .Clock(clock_1_out), .RAM_BUS(MDRM));
  Button Reset_PC (.out(Reset_PC_out));
  MAR mar_1 (.In(buffer_3_out), .Out(mar_1_out), .Load(MARI), .Enable(MARO), .State(MAR), .Clock(clock_1_out));
  RAM #(.addrWidth(16), .bus("separate")) ram_1 (
    .addr(mar_1_out), .din(mdr_1_ramout), .data(ram_1_data), .str(RI), .clk(clock_1_out), .ld(RO));  // open: sel, clr
  InstructionRegister instructionregister_1 (
    .In(buffer_6_out), .out_4(Instruction_Register), .L(IRI), .Clk(clock_1_out));
  Control_Logic control_logic_1 (
    .IR(Instruction_Register), .ControlOut(control_logic_1_controlout), .Clk(clock_1_out), .Step(out_41),
    .RES(CLR), .ZF(ZF), .NF(NF));
  assign Bus = programcounter_1_out_2;  // Buffer buffer_1, 16 bits wide
  ProgramCounter programcounter_1 (
    .Load(PCI), .in_2(buffer_2_out), .Increment(PCA), .Out_2(programcounter_1_out_2),
    .out_7(Program_Counter), .Clock(clock_1_out), .Out(PCO), .reset(Reset_PC_out));
  assign buffer_2_out = Bus;  // Buffer buffer_2, 16 bits wide
  assign buffer_3_out = Bus;  // Buffer buffer_3, 16 bits wide
  assign Bus = mdr_1_busout;  // Buffer buffer_4, 16 bits wide
  assign buffer_5_out = Bus;  // Buffer buffer_5, 16 bits wide
  assign buffer_6_out = Bus;  // Buffer buffer_6, 16 bits wide
  not not_1 (not_1_out, Manual);
  assign {PCI, PCA, PCO, MARI, MARO, RI, RO, MDRI, MDRM, MDRO, IRI, CLR, AO, AI, ALUM, ALUC, ALUO, TO, TI, BO, BI, CO, CI, DO, DCLR, H} = not_1_out ? control_logic_1_controlout : 29'bz;  // Controlled_Buffer controlled_buffer_27
  Pull_Resistor pull_resistor_1 (.node(Bus));
  assign buffer_7_out = Bus;  // Buffer buffer_7, 16 bits wide
  assign Bus = in_2 ? Tester : 16'bz;  // Controlled_Buffer controlled_buffer_28
  assign Bus = n16_bit_register_1_out;  // Buffer buffer_8, 16 bits wide
  assign buffer_9_out = Bus;  // Buffer buffer_9, 16 bits wide
  assign Bus = alu_1_output;  // Buffer buffer_10, 16 bits wide
  ALU alu_1 (.Enable(ALUO), .A(Accumulator), .M(ALUM), .Output(alu_1_output), .B(TMP), .in_5(ALUC), .S(ALU_Output));
  assign Bus = n16_bit_register_2_out;  // Buffer buffer_11, 16 bits wide
  assign buffer_12_out = Bus;  // Buffer buffer_12, 16 bits wide
  assign Bus = n16_bit_register_3_out;  // Buffer buffer_13, 16 bits wide
  assign buffer_14_out = Bus;  // Buffer buffer_14, 16 bits wide
  assign Bus = n16_bit_register_4_out;  // Buffer buffer_15, 16 bits wide
  assign buffer_16_out = Bus;  // Buffer buffer_16, 16 bits wide
  _8_bit_Display Output (
    .In(buffer_7_out), .BCD(Output_bcd), .LSB(Output_lsb), .MSB(Output_msb), .Enable(DO),
    .Clock(clock_1_out), .Clear(DCLR));
  _16_bit_Register u_16_bit_register_1 (
    .In(buffer_9_out), .Load(AI), .State(Accumulator), .Out(n16_bit_register_1_out), .Clock(clock_1_out),
    .Enable(AO));
  _16_bit_Register u_16_bit_register_2 (
    .In(buffer_12_out), .Load(TI), .State(TMP), .Out(n16_bit_register_2_out), .Clock(clock_1_out), .Enable(TO));
  _16_bit_Register u_16_bit_register_3 (
    .In(buffer_14_out), .Load(BI), .State(B), .Out(n16_bit_register_3_out), .Clock(clock_1_out), .Enable(BO));
  _16_bit_Register u_16_bit_register_4 (
    .In(buffer_16_out), .Load(CI), .State(C), .Out(n16_bit_register_4_out), .Clock(clock_1_out), .Enable(CO));
  Button Pulse (.out(Pulse_out));
  Clock clock_1 (.Pulse(Pulse_out), .Enable(in_1), .Out(clock_1_out), .HLT(H));
  Flags Flags (.In(ALU_Output), .ZERO(ZF), .NEG(NF), .Clock(clock_1_out));
  _7_Segment_Display u_7_segment_display_1 (
    .g(Output_bcd[19]), .f(Output_bcd[18]), .a(Output_bcd[17]), .b(Output_bcd[16]), .e(Output_bcd[23]),
    .d(Output_bcd[22]), .c(Output_bcd[21]), .dp(Output_bcd[20]));
  _7_Segment_Display u_7_segment_display_2 (
    .g(Output_bcd[27]), .f(Output_bcd[26]), .a(Output_bcd[25]), .b(Output_bcd[24]), .e(Output_bcd[31]),
    .d(Output_bcd[30]), .c(Output_bcd[29]), .dp(Output_bcd[28]));
  Hex_Digit_Display hex_digit_display_1 (.value(Output_msb));  // open: dp
  _7_Segment_Display u_7_segment_display_3 (
    .g(Output_bcd[11]), .f(Output_bcd[10]), .a(Output_bcd[9]), .b(Output_bcd[8]), .e(Output_bcd[15]),
    .d(Output_bcd[14]), .c(Output_bcd[13]), .dp(Output_bcd[12]));
  _7_Segment_Display u_7_segment_display_4 (
    .g(Output_bcd[3]), .f(Output_bcd[2]), .a(Output_bcd[1]), .b(Output_bcd[0]), .e(Output_bcd[7]),
    .d(Output_bcd[6]), .c(Output_bcd[5]), .dp(Output_bcd[4]));
  Hex_Digit_Display hex_digit_display_2 (.value(Output_lsb));  // open: dp

  // Notes on the sheet:
  //   SAP-II 
  //   HEX
endmodule

module Clock (
  input  Pulse,
  input  Enable,
  input  HLT,
  output Out
);

  wire and_1_out, and_2_out, Clock_out, not_1_out, not_2_out, or_1_out;

  Clock_part Clock (.out(Clock_out));
  and and_1 (and_1_out, Clock_out, Enable);
  and and_2 (and_2_out, Pulse, not_1_out);
  not not_1 (not_1_out, Enable);
  Pull_Resistor pull_resistor_1 (.node(Out));
  assign Out = not_2_out ? or_1_out : 1'bz;  // Controlled_Buffer controlled_buffer_1
  or or_1 (or_1_out, and_1_out, and_2_out);
  not not_2 (not_2_out, HLT);
endmodule

module _16_bit_Register (
  input  [15:0] In,
  input  Clock,
  input  Load,
  input  Enable,
  output [7:0] State,
  output [15:0] Out
);

  wire [7:0] bitselector_1_out, controlled_buffer_1_out;
  wire [15:0] bitselector_2_out;

  BitSelector #(.width(16), .group(8)) bitselector_1 (.in(In), .out(bitselector_1_out), .sel(1'b0));
  assign controlled_buffer_1_out = Load ? bitselector_1_out : 8'bz;  // Controlled_Buffer controlled_buffer_1
  Register register_1 (.D(controlled_buffer_1_out), .Q(State), .clk(Clock));  // open: en, clr
  BitSelector #(.group(16)) bitselector_2 (.in(State), .out(bitselector_2_out), .sel(1'b0));
  assign Out = Enable ? bitselector_2_out : 16'bz;  // Controlled_Buffer controlled_buffer_2
endmodule

module ALU (
  input  [7:0] A,
  input  M,
  input  [7:0] B,
  input  Enable,
  input  [3:0] in_5,
  output [7:0] S,
  output [15:0] Output
);

  wire and_2_out, and_3_out, and_4_out;
  wire [3:0] xnor_1_out, xnor_2_out, xnor_3_out;
  wire [7:0] adder_1_out, adder_2_out, and_1_out, controlled_buffer_2_out, controlled_buffer_3_out,
       nor_1_out, not_1_out, or_1_out, subtractor_1_out, xor_1_out, xor_2_out;
  wire [15:0] bitselector_1_out, bitselector_2_out, bitselector_3_out, controlled_buffer_1_out, or_2_out;

  Adder adder_1 (.a(B), .b(8'h1), .out(adder_1_out));  // open: cin, cout
  Subtractor subtractor_1 (.a(B), .b(8'h1), .out(subtractor_1_out));  // open: bin, bout
  assign xor_1_out = {8{M}} ^ B;  // XOR_Gate xor_1, 8 bits wide
  assign and_1_out = A & B;  // AND_Gate and_1, 8 bits wide
  assign or_1_out = A | B;  // OR_Gate or_1, 8 bits wide
  assign xor_2_out = A ^ B;  // XOR_Gate xor_2, 8 bits wide
  assign nor_1_out = ~(A | B);  // NOR_Gate nor_1, 8 bits wide
  assign not_1_out = ~A;  // NOT_Gate not_1, 8 bits wide
  Adder adder_2 (.a(A), .b(xor_1_out), .out(adder_2_out), .cin(M));  // open: cout
  Multiplexer #(.select(4), .width(8)) multiplexer_1 (
    .in0(and_1_out), .in1(or_1_out), .in2(xor_2_out), .in3(nor_1_out), .in4(adder_2_out), .in5(not_1_out),
    .in6(adder_1_out), .in7(subtractor_1_out), .out(S), .sel(in_5), .en(1'b1));  // open: in8, in9, in10, in11, in12, in13, in14, in15
  assign xnor_1_out = ~(4'b1000 ^ in_5);  // XNOR_Gate xnor_1, 4 bits wide
  assign xnor_2_out = ~(4'b1010 ^ in_5);  // XNOR_Gate xnor_2, 4 bits wide
  assign xnor_3_out = ~(4'b1001 ^ in_5);  // XNOR_Gate xnor_3, 4 bits wide
  and and_2 (and_2_out, xnor_1_out[0], xnor_1_out[1], xnor_1_out[2], xnor_1_out[3]);
  and and_3 (and_3_out, xnor_2_out[0], xnor_2_out[1], xnor_2_out[2], xnor_2_out[3]);
  and and_4 (and_4_out, xnor_3_out[0], xnor_3_out[1], xnor_3_out[2], xnor_3_out[3]);
  BitSelector #(.group(16)) bitselector_1 (.in(S), .out(bitselector_1_out), .sel(1'b0));
  assign controlled_buffer_1_out = and_2_out ? {A, B} : 16'bz;  // Controlled_Buffer controlled_buffer_1
  Pull_Resistor pull_resistor_1 (.node(controlled_buffer_1_out));
  Pull_Resistor pull_resistor_2 (.node(bitselector_1_out));
  BitSelector #(.group(16)) bitselector_2 (.in(controlled_buffer_2_out), .out(bitselector_2_out), .sel(1'b0));
  assign controlled_buffer_2_out = and_3_out ? {B[0], B[7:1]} : 8'bz;  // Controlled_Buffer controlled_buffer_2
  Pull_Resistor pull_resistor_3 (.node(bitselector_2_out));
  assign controlled_buffer_3_out = and_4_out ? {B[6:0], B[7]} : 8'bz;  // Controlled_Buffer controlled_buffer_3
  BitSelector #(.group(16)) bitselector_3 (.in(controlled_buffer_3_out), .out(bitselector_3_out), .sel(1'b0));
  Pull_Resistor pull_resistor_4 (.node(bitselector_3_out));
  assign or_2_out = bitselector_1_out | bitselector_2_out | bitselector_3_out | controlled_buffer_1_out;  // OR_Gate or_2, 16 bits wide
  assign Output = Enable ? or_2_out : 16'bz;  // Controlled_Buffer controlled_buffer_4

  // Notes on the sheet:
  //   0-AND/1-OR/2-XOR/3-NOR/4/DD-SUB/5-CMA/6-INC/7-DCR/8-LDA/9-ROTL/10-ROTR/STA
  //   LDA
  //   ROTR
  //   ROTL
endmodule

module _8_bit_Display (
  input  [15:0] In,
  input  Enable,
  input  Clock,
  input  Clear,
  output [31:0] BCD,
  output [3:0] LSB,
  output [3:0] MSB
);

  wire [7:0] bitselector_1_out, controlled_buffer_1_out, register_1_q;

  BitSelector #(.width(16), .group(8)) bitselector_1 (.in(In), .out(bitselector_1_out), .sel(1'b0));
  assign controlled_buffer_1_out = Enable ? bitselector_1_out : 8'bz;  // Controlled_Buffer controlled_buffer_1
  Register register_1 (.D(controlled_buffer_1_out), .Q(register_1_q), .clk(Clock), .clr(Clear));  // open: en
  BitSelector #(.group(4)) bitselector_2 (.in(register_1_q), .out(LSB), .sel(1'b0));
  BitSelector #(.group(4)) bitselector_3 (.in(register_1_q), .out(MSB), .sel(1'b1));
  ROM #(.addrWidth(9), .dataWidth(32)) rom_1 (.addr({1'b1, register_1_q}), .data(BCD));  // open: sel

  // Notes on the sheet:
  //   contents of rom_1 (hex, n*v repeats v):
  //   e7 21 cb 6b 2d 6e ee 23 ef 6f 21e7 2121 21cb 216b 212d 216e 21ee 2123 21ef 216f cbe7 cb21 cbcb cb6b
  //   cb2d cb6e cbee cb23 cbef cb6f 6be7 6b21 6bcb 6b6b 6b2d 6b6e 6bee 6b23 6bef 6b6f 2de7 2d21 2dcb 2d6b
  //   2d2d 2d6e 2dee 2d23 2def 2d6f 6ee7 6e21 6ecb 6e6b 6e2d 6e6e 6eee 6e23 6eef 6e6f eee7 ee21 eecb ee6b
  //   ee2d ee6e eeee ee23 eeef ee6f 23e7 2321 23cb 236b 232d 236e 23ee 2323 23ef 236f efe7 ef21 efcb ef6b
  //   ef2d ef6e efee ef23 efef ef6f 6fe7 6f21 6fcb 6f6b 6f2d 6f6e 6fee 6f23 6fef 6f6f 21e7e7 21e721 21e7cb
  //   21e76b 21e72d 21e76e 21e7ee 21e723 21e7ef 21e76f 2121e7 212121 2121cb 21216b 21212d 21216e 2121ee
  //   212123 2121ef 21216f 21cbe7 21cb21 21cbcb 21cb6b 21cb2d 21cb6e 21cbee 21cb23 21cbef 21cb6f 216be7
  //   216b21 216bcb 216b6b 216b2d 216b6e 216bee 216b23 216bef 216b6f 212de7 212d21 212dcb 212d6b 212d2d
  //   212d6e 212dee 212d23 212def 212d6f 216ee7 216e21 216ecb 216e6b 216e2d 216e6e 216eee 216e23 216eef
  //   216e6f 21eee7 21ee21 21eecb 21ee6b 21ee2d 21ee6e 21eeee 21ee23 21eeef 21ee6f 2123e7 212321 2123cb
  //   21236b 21232d 21236e 2123ee 212323 2123ef 21236f 21efe7 21ef21 21efcb 21ef6b 21ef2d 21ef6e 21efee
  //   21ef23 21efef 21ef6f 216fe7 216f21 216fcb 216f6b 216f2d 216f6e 216fee 216f23 216fef 216f6f cbe7e7
  //   cbe721 cbe7cb cbe76b cbe72d cbe76e cbe7ee cbe723 cbe7ef cbe76f cb21e7 cb2121 cb21cb cb216b cb212d
  //   cb216e cb21ee cb2123 cb21ef cb216f cbcbe7 cbcb21 cbcbcb cbcb6b cbcb2d cbcb6e cbcbee cbcb23 cbcbef
  //   cbcb6f cb6be7 cb6b21 cb6bcb cb6b6b cb6b2d cb6b6e cb6bee cb6b23 cb6bef cb6b6f cb2de7 cb2d21 cb2dcb
  //   cb2d6b cb2d2d cb2d6e cb2dee cb2d23 cb2def cb2d6f cb6ee7 cb6e21 cb6ecb cb6e6b cb6e2d cb6e6e e7 21 cb
  //   6b 2d 6e ee 23 ef 6f 21e7 2121 21cb 216b 212d 216e 21ee 2123 21ef 216f cbe7 cb21 cbcb cb6b cb2d cb6e
  //   cbee cb23 cbef cb6f 6be7 6b21 6bcb 6b6b 6b2d 6b6e 6bee 6b23 6bef 6b6f 2de7 2d21 2dcb 2d6b 2d2d 2d6e
  //   2dee 2d23 2def 2d6f 6ee7 6e21 6ecb 6e6b 6e2d 6e6e 6eee 6e23 6eef 6e6f eee7 ee21 eecb ee6b ee2d ee6e
  //   eeee ee23 eeef ee6f 23e7 2321 23cb 236b 232d 236e 23ee 2323 23ef 236f efe7 ef21 efcb ef6b ef2d ef6e
  //   efee ef23 efef ef6f 6fe7 6f21 6fcb 6f6b 6f2d 6f6e 6fee 6f23 6fef 6f6f 21e7e7 21e721 21e7cb 21e76b
  //   21e72d 21e76e 21e7ee 21e723 21e7ef 21e76f 2121e7 212121 2121cb 21216b 21212d 21216e 2121ee 212123
  //   2121ef 21216f 21cbe7 21cb21 21cbcb 21cb6b 21cb2d 21cb6e 21cbee 21cb23 821cbef 821cb23 821cbee
  //   821cb6e 821cb2d 821cb6b 821cbcb 821cb21 821cbe7 821216f 82121ef 8212123 82121ee 821216e 821212d
  //   821216b 82121cb 8212121 82121e7 821e76f 821e7ef 821e723 821e7ee 821e76e 821e72d 821e76b 821e7cb
  //   821e721 821e7e7 8006f6f 8006fef 8006f23 8006fee 8006f6e 8006f2d 8006f6b 8006fcb 8006f21 8006fe7
  //   800ef6f 800efef 800ef23 800efee 800ef6e 800ef2d 800ef6b 800efcb 800ef21 800efe7 800236f 80023ef
  //   8002323 80023ee 800236e 800232d 800236b 80023cb 8002321 80023e7 800ee6f 800eeef 800ee23 800eeee
  //   800ee6e 800ee2d 800ee6b 800eecb 800ee21 800eee7 8006e6f 8006eef 8006e23 8006eee 8006e6e 8006e2d
  //   8006e6b 8006ecb 8006e21 8006ee7 8002d6f 8002def 8002d23 8002dee 8002d6e 8002d2d 8002d6b 8002dcb
  //   8002d21 8002de7 8006b6f 8006bef 8006b23 8006bee 8006b6e 8006b2d 8006b6b 8006bcb 8006b21 8006be7
  //   800cb6f 800cbef 800cb23 800cbee 800cb6e 800cb2d 800cb6b 800cbcb 800cb21 800cbe7 800216f 80021ef
  //   8002123 80021ee 800216e 800212d 800216b 80021cb 8002121 80021e7 800006f 80000ef 8000023 80000ee
  //   800006e 800002d 800006b 80000cb 8000021
endmodule

module ProgramCounter (
  input  Load,
  input  [15:0] in_2,
  input  Increment,
  input  reset,
  input  Out,
  input  Clock,
  output [15:0] out_7,
  output [15:0] Out_2
);

  Counter #(.width(16), .max('hffff)) counter_1 (
    .load(Load), .D(in_2), .count(Increment), .Q(out_7), .clk(Clock), .clr(reset));  // open: carry
  assign Out_2 = Out ? out_7 : 16'bz;  // Controlled_Buffer controlled_buffer_1
endmodule

module MAR (
  input  [15:0] In,
  input  Clock,
  input  Load,
  input  Enable,
  output [15:0] State,
  output [15:0] Out
);

  wire [15:0] controlled_buffer_1_out;

  assign controlled_buffer_1_out = Load ? In : 16'bz;  // Controlled_Buffer controlled_buffer_1
  Register #(.width(16)) register_1 (.D(controlled_buffer_1_out), .Q(State), .clk(Clock));  // open: en, clr
  assign Out = Enable ? State : 16'bz;  // Controlled_Buffer controlled_buffer_2
endmodule

module Selector (
  input  [15:0] MAR16,
  input  [7:0] MAR8,
  input  [15:0] IN16,
  input  in_4,
  output [15:0] out_5,
  output [7:0] out_6,
  output [15:0] out_7
);

  wire not_1_out;

  not not_1 (not_1_out, in_4);
  assign out_5 = not_1_out ? MAR16 : 16'bz;  // Controlled_Buffer _4
  assign out_6 = not_1_out ? MAR8 : 8'bz;  // Controlled_Buffer _8
  assign out_7 = in_4 ? IN16 : 16'bz;  // Controlled_Buffer _4_2
endmodule

module MDR (
  input  [15:0] BUSIn,
  input  [7:0] RAMIn,
  input  Clock,
  input  Load,
  input  Enable,
  input  RAM_BUS,
  output [15:0] BUSOut,
  output [7:0] State,
  output [7:0] RAMOut
);

  wire not_1_out, not_2_out;
  wire [7:0] bitselector_1_out, controlled_buffer_1_out, controlled_buffer_3_out, controlled_buffer_4_out,
       controlled_buffer_5_out;

  BitSelector #(.width(16), .group(8)) bitselector_1 (.in(BUSIn), .out(bitselector_1_out), .sel(1'b0));
  assign controlled_buffer_1_out = RAM_BUS ? bitselector_1_out : 8'bz;  // Controlled_Buffer controlled_buffer_1
  assign controlled_buffer_1_out = not_1_out ? RAMIn : 8'bz;  // Controlled_Buffer controlled_buffer_2
  not not_1 (not_1_out, RAM_BUS);
  Register register_1 (.D(controlled_buffer_3_out), .Q(State), .clk(Clock));  // open: en, clr
  assign controlled_buffer_3_out = Load ? controlled_buffer_1_out : 8'bz;  // Controlled_Buffer controlled_buffer_3
  assign controlled_buffer_4_out = Enable ? State : 8'bz;  // Controlled_Buffer controlled_buffer_4
  assign controlled_buffer_5_out = RAM_BUS ? controlled_buffer_4_out : 8'bz;  // Controlled_Buffer controlled_buffer_5
  BitSelector #(.group(16)) bitselector_2 (.in(controlled_buffer_5_out), .out(BUSOut), .sel(1'b0));
  assign RAMOut = not_2_out ? controlled_buffer_4_out : 8'bz;  // Controlled_Buffer controlled_buffer_6
  not not_2 (not_2_out, RAM_BUS);
endmodule

module InstructionRegister (
  input  [15:0] In,
  input  L,
  input  Clk,
  output [7:0] out_4
);

  wire [7:0] bitselector_1_out, controlled_buffer_1_out;

  BitSelector #(.width(16), .group(8)) bitselector_1 (.in(In), .out(bitselector_1_out), .sel(1'b0));
  Register register_1 (.D(controlled_buffer_1_out), .Q(out_4), .clk(Clk));  // open: en, clr
  assign controlled_buffer_1_out = L ? bitselector_1_out : 8'bz;  // Controlled_Buffer controlled_buffer_1
endmodule

module Control_Logic (
  input  ZF,
  input  NF,
  input  Clk,
  input  RES,
  input  [7:0] IR,
  output [28:0] ControlOut,
  output [3:0] Step
);

  wire decoder_1_out15, not_1_out, or_1_out;

  Decoder #(.select(4)) decoder_1 (
    .out15(decoder_1_out15), .sel(Step), .en(1'b1));  // open: out0, out1, out2, out3, out4, out5, out6, out7, out8, out9, out10, out11, out12, out13, out14
  Counter #(.width(4), .max('hf)) counter_1 (
    .count(1'b1), .Q(Step), .clk(not_1_out), .clr(or_1_out));  // open: load, D, carry
  not not_1 (not_1_out, Clk);
  or or_1 (or_1_out, decoder_1_out15, RES);
  ROM #(.addrWidth(14), .dataWidth(29)) rom_1 (.addr({IR, NF, ZF, Step}), .data(ControlOut));  // open: sel

  // Notes on the sheet:
  //   contents of rom_1 (hex, n*v repeats v):
  //   7600000 7600000 81c0000 13*0 7600000 7600000 81c0000 13*0 7600000 7600000 81c0000 13*0 7600000
  //   7600000 81c0000 205*0 7600000 7600000 81c0000 c0 1a20 20000 10*0 7600000 7600000 81c0000 c0 1a20
  //   20000 10*0 7600000 7600000 81c0000 c0 1a20 20000 10*0 7600000 7600000 81c0000 c0 1a20 20000 10*0
  //   7600000 7600000 81c0000 c0 1e20 20000 10*0 7600000 7600000 81c0000 c0 1e20 20000 10*0 7600000
  //   7600000 81c0000 c0 1e20 20000 10*0 7600000 7600000 81c0000 c0 1e20 20000 10*0 7600000 7600000
  //   81c0000 7600000 7600000 8180020 20000 9*0 7600000 7600000 81c0000 7600000 7600000 8180020 20000 9*0
  //   7600000 7600000 81c0000 7600000 7600000 8180020 20000 9*0 7600000 7600000 81c0000 7600000 7600000
  //   8180020 20000 329*0 7600000 7600000 81c0000 90 1a08 20000 10*0 7600000 7600000 81c0000 90 1a08 20000
  //   10*0 7600000 7600000 81c0000 90 1a08 20000 10*0 7600000 7600000 81c0000 90 1a08 20000 10*0 7600000
  //   7600000 81c0000 90 1e08 20000 10*0 7600000 7600000 81c0000 90 1e08 20000 10*0 7600000 7600000
  //   81c0000 90 1e08 20000 10*0 7600000 7600000 81c0000 90 1e08 20000 10*0 7600000 7600000 81c0000
  //   7600000 7600000 8180008 20000 9*0 7600000 7600000 81c0000 7600000 7600000 8180008 20000 9*0 7600000
  //   7600000 81c0000 7600000 7600000 8180008 20000 9*0 7600000 7600000 81c0000 7600000 7600000 8180008
  //   20000 521*0 7600000 7600000 81c0000 10080 a600 20000 10*0 7600000 7600000 81c0000 10080 a600 20000
  //   10*0 7600000 7600000 81c0000 10080 a600 20000 10*0 7600000 7600000 81c0000 10080 a600 20000 458*0
  //   7600000 0 81c0000 10080 aa00 20000 10*0 7600000 7600000 81c0000 10080 aa00 20000 10*0 7600000
  //   7600000 81c0000 10080 aa00 20000 10*0 7600000 7600000 81c0000 10080 aa00 20000 970*0 7600000 7600000
  //   81c0000 9600 20000 0 0 20000 8*0 7600000 7600000 81c0000 9600 20000 0 0 20000 8*0 7600000 7600000
  //   81c0000 9600 20000 0 0 20000 8*0 7600000 7600000 81c0000 9600 20000 0 0 20000 648*0 7600000 7600000
  //   81c0000 7600000 7600000 8180020 7600000 7600000 188000 b602200 3600000 188000 20000 0 0 0 7600000
  //   7600000 81c0000 7600000 7600000 8180020 7600000 7600000 188000 b602200 3600000 188000 20000 0 0 0
  //   7600000 7600000 81c0000 7600000 7600000 8180020 7600000 7600000 188000 b602200 3600000 188000 20000
  //   0 0 0 7600000 7600000 81c0000 7600000 7600000 8180020 7600000 7600000 188000 b602200 3600000 188000
  //   20000 67*0 7600000 7600000 81c0000 10080 9a00 20000 10*0 7600000 7600000 81c0000 10080 9a00 20000
  //   10*0 7600000 7600000 81c0000 10080 9a00 20000 10*0 7600000 7600000 81c0000 10080 9a00 20000 10*0
  //   7600000 7600000 81c0000 10080 9e00 20000 10*0 7600000 7600000 81c0000 10080 9e00 20000 10*0 7600000
  //   0 81c0000 10080 9e00 20000 10*0 7600000 7600000 81c0000 10080 9e00 20000 10*0 7600000 7600000
  //   81c0000 7600000 7600000 8188000 20000 9*0 7600000 7600000 81c0000 7600000 7600000 8188000 20000 9*0
  //   7600000 7600000 81c0000 7600000 7600000 8188000 20000 9*0 7600000 7600000 81c0000 7600000 7600000
  //   8188000 20000 137*0 7600000 7600000 81c0000 30 20000 11*0 7600000 7600000 81c0000 30 20000 11*0
  //   7600000 7600000 81c0000 30 20000 11*0 7600000 7600000 81c0000 30 20000 331*0 7600000 7600000 81c0000
  //   8010 20000 11*0 7600000 7600000 81c0000 8010 20000 11*0 7600000 7600000 81c0000 8010 20000 11*0
  //   7600000 7600000 81c0000 8010 20000 11*0 7600000 7600000 81c0000 48 20000 11*0 7600000 7600000
  //   81c0000 48 20000 11*0 7600000 7600000 81c0000 48 20000 11*0 7600000 7600000 81c0000 48 20000 395*0
  //   7600000 7600000 81c0000 10008 20000 11*0 7600000 7600000 81c0000 10008 20000 11*0 7600000 7600000
  //   81c0000 10008 20000 11*0 7600000 7600000 81c0000 10008 20000 2443*0 7600000 7600000 81c0000 1 12*0
  //   7600000 7600000 81c0000 1 12*0 7600000 7600000 81c0000 1 12*0 7600000 7600000 81c0000 1 76*0 7600000
  //   7600000 81c0000 8040 20000 12*0 7600000 81c0000 8040 20000 11*0 7600000 7600000 81c0000 8040 20000
  //   11*0 7600000 7600000 81c0000 8040 20000 11*0 7600000 7600000 81c0000 8010 20000 11*0 7600000 7600000
  //   81c0000 8010 20000 11*0 7600000 7600000 81c0000 8010 20000 11*0 7600000 7600000 81c0000 8010 20000
  //   395*0 7600000 7600000 81c0000 c0 9200 20000 10*0 7600000 7600000 81c0000 c0 9200 20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
endmodule

module Flags (
  input  [7:0] In,
  input  Clock,
  output ZERO,
  output NEG
);

  wire nor_1_out;

  nor nor_1 (nor_1_out, In[0], In[1], In[2], In[3], In[4], In[5], In[6], In[7]);
  Register #(.width(1)) register_1 (.D(nor_1_out), .Q(ZERO), .clk(Clock));  // open: en, clr
  Register #(.width(1)) register_2 (.D(In[7]), .Q(NEG), .clk(Clock));  // open: en, clr
endmodule

module InstructionSetProgrammer (
  input  [7:0] in_1,
  input  [1:0] in_2,
  input  [3:0] in_3,
  input  [4:0] in_4,
  input  [7:0] in_5,
  input  [7:0] in_6,
  input  [7:0] in_7
);

  wire button_1_out;

  Button button_1 (.out(button_1_out));
  RAM #(.addrWidth(14), .dataWidth(29), .bus("separate")) ram_1 (
    .addr({in_1, in_2, in_3}), .din({in_4, in_5, in_6, in_7}), .str(button_1_out), .clk(button_1_out));  // open: data, sel, ld, clr
endmodule
